// Logisim project rook.circ as structural Verilog: 1 circuit, main circuit main
module main (
  input  P,
  input  x2,
  input  x1,
  input  x0,
  input  y2,
  input  y1,
  input  y0,
  output left,
  output rght,
  output [2:0] X_out,
  output down,
  output up,
  output [2:0] Y_out
);

  wire a0_qn, a1_qn, and_1_out, and_2_out, and_3_out, and_4_out, and_5_out, and_6_out, and_7_out, and_8_out,
       b0_qn, b1_qn, clock_1_out, comparator_1_eq, comparator_2_eq, not_1_out, not_2_out, not_3_out,
       not_4_out, not_5_out, not_6_out, or_1_out, or_2_out, undriven;
  wire [1:0] priority_encoder_1_out, priority_encoder_2_out;

  Comparator #(.width(3), .mode("unsigned")) comparator_1 (
    .a(X_out), .b({x2, x1, x0}), .gt(left), .eq(comparator_1_eq), .lt(rght));
  not not_1 (not_1_out, comparator_2_eq);
  Comparator #(.width(3), .mode("unsigned")) comparator_2 (
    .a(Y_out), .b({y2, y1, y0}), .gt(down), .eq(comparator_2_eq), .lt(up));
  Priority_Encoder #(.select(2)) priority_encoder_1 (
    .in0(left), .in1(comparator_1_eq), .in2(rght), .in3(not_1_out), .out(priority_encoder_1_out));  // open: gs, en_out, en_in
  not not_2 (not_2_out, comparator_1_eq);
  Priority_Encoder #(.select(2)) priority_encoder_2 (
    .in0(down), .in1(comparator_2_eq), .in2(up), .in3(not_2_out), .out(priority_encoder_2_out));  // open: gs, en_out, en_in
  not not_3 (not_3_out, priority_encoder_1_out[0]);
  not not_4 (not_4_out, priority_encoder_1_out[1]);
  not not_5 (not_5_out, priority_encoder_2_out[0]);
  not not_6 (not_6_out, priority_encoder_2_out[1]);
  and and_1 (and_1_out, priority_encoder_1_out[1], not_3_out, X_out[0]);
  and and_2 (and_2_out, not_4_out, not_3_out, a0_qn);
  and and_3 (and_3_out, priority_encoder_2_out[1], not_5_out, Y_out[0]);
  and and_4 (and_4_out, not_6_out, not_5_out, b0_qn);
  or or_1 (or_1_out, and_1_out, and_2_out);
  or or_2 (or_2_out, and_3_out, and_4_out);
  Clock clock_1 (.out(clock_1_out));
  and and_5 (and_5_out, and_1_out, X_out[1]);
  and and_6 (and_6_out, a1_qn, and_2_out);
  and and_7 (and_7_out, and_3_out, Y_out[1]);
  and and_8 (and_8_out, b1_qn, and_4_out);
  J_K_Flip_Flop a2 (.J(and_5_out), .clk(clock_1_out), .K(and_6_out), .Q(X_out[2]));  // open: Qn, preset, en, reset
  J_K_Flip_Flop a1 (
    .J(or_1_out), .clk(clock_1_out), .K(or_1_out), .Q(X_out[1]), .Qn(a1_qn));  // open: preset, en, reset
  J_K_Flip_Flop a0 (
    .J(not_3_out), .clk(clock_1_out), .K(not_3_out), .Q(X_out[0]), .Qn(a0_qn), .en(undriven), .reset(undriven));  // open: preset
  J_K_Flip_Flop b2 (.J(and_7_out), .clk(clock_1_out), .K(and_8_out), .Q(Y_out[2]));  // open: Qn, preset, en, reset
  J_K_Flip_Flop b1 (
    .J(or_2_out), .clk(clock_1_out), .K(or_2_out), .Q(Y_out[1]), .Qn(b1_qn));  // open: preset, en, reset
  J_K_Flip_Flop b0 (
    .J(not_5_out), .clk(clock_1_out), .K(not_5_out), .Q(Y_out[0]), .Qn(b0_qn));  // open: preset, en, reset
endmodule
